# Fritzing sketch mega-toggle-led (saved by Fritzing 0.9.3b)
breadboards: 1

parts:
  Part1 = Arduino Mega 2560 (Rev3)
  LED1 = LED - 5mm [color="White (4500K)" package="5 mm [THT]"]
  R1 = Resistor [tolerance=±5% resistance=1k package=THT]
  S1 = Pushbutton [package="[THT]"]

nets:
  N1: Part1.GND, LED1.cathode, S1.Pin_1, S1.Pin_2
  N2: Part1.D12_PWM, R1.Pin_1
  N3: Part1.D9_PWM, S1.Pin_3, S1.Pin_4
  N4: LED1.anode, R1.Pin_0

// code stored in the sketch: mega-toggled-led.ino
int ledPin = 12;
int buttonPin = 9;
int toggleState = false;

void setup()
{
  pinMode(ledPin, OUTPUT);
  pinMode(buttonPin, INPUT_PULLUP);
}

void loop()
{
  if (digitalRead(buttonPin) == false) {
  toggleState = !toggleState;
  digitalWrite(ledPin, toggleState);
  }
  while (digitalRead(buttonPin) == false);
  delay(50);
}
