# Fritzing sketch arduino-led-encoder-servo (saved by Fritzing 0.9.3b)
circuit board: 8.46667cm x 5.64444cm
breadboards: 1

parts:
  Part1 = Arduino Mega 2560 (Rev3)
  R1 = Resistor [tolerance=±5% resistance=220 package=THT]
  LED1 = LED - 5mm [color="Red (633nm)" package="5 mm [THT]"]
  SERVO1 = Tower Pro SG90 servo [part_number=101246]
  SW1 = ENCODER_RGB_CA [package=encoder_led_3]

nets (from the breadboard view):
  N1: Part1.D11_PWM, R1.Pin_1
  N2: Part1.D9_PWM, SERVO1.Signal
  5V: Part1.5V, SERVO1.+5V, SW1.+
  GND: Part1.GND, LED1.cathode, SERVO1.GND, SW1.-B
  N3: Part1.D2_PWM, SW1.C
  N4: Part1.D3_PWM, SW1.B
  N5: Part1.D4_PWM, SW1.A
  N6: R1.Pin_0, LED1.anode
  N7: SW1.-R, SW1.-G, SW1.SW

custom parts:
  Tower Pro SG90 servo: Original file by John De Cristofaro http://www.adafruit.com/products/1449 Adafruit Feedback Servo (Small) Edited by: e-radionica.com 28/9/2015
