# Fritzing sketch tapuino (saved by Fritzing 0.9.4)
breadboards: 1

parts:
  Arduino_Nano_V3 = Arduino Nano (Rev3.0)
  U1 = LCD-16X2 [package=lcd-16x2]
  LCM1602_IIC2 = LCM1602 IIC [part_number="LCM1602 IIC" chip_label="LCM1602 IIC" package="DIP (Dual Inline) [THT]"]
  4N25 = 4N25 [package=THT]
  Part2 = MicroSD Card Module
  part = Resistor [tolerance=±5% resistance=430 package=THT]
  S1 = Momentary Switch [package=ksa_sealed_tac_switch]
  S2 = Momentary Switch [package=ksa_sealed_tac_switch]
  S2_2 = Momentary Switch [package=ksa_sealed_tac_switch]
  S1_2 = Momentary Switch [package=ksa_sealed_tac_switch]

nets:
  GND: Arduino_Nano_V3.GND, LCM1602_IIC2.GND, 4N25.Pin_2, 4N25.Pin_4, Part2.GND, S1.1, S2.1, S2_2.1, S1_2.1
  N1: Arduino_Nano_V3.D4, 4N25.Pin_5
  N2: Arduino_Nano_V3.D10, Part2.CS
  N3: Arduino_Nano_V3.D11/MOSI, Part2.MOSI
  N4: Arduino_Nano_V3.D12/MISO, Part2.SCK
  VCC: Arduino_Nano_V3.5V, LCM1602_IIC2.VCC, Part2.VCC
  N5: Arduino_Nano_V3.A5, LCM1602_IIC2.SDA
  N6: Arduino_Nano_V3.A4, LCM1602_IIC2.SCL
  N7: Arduino_Nano_V3.A3, S1_2.3
  N8: Arduino_Nano_V3.A2, S2_2.3
  N9: Arduino_Nano_V3.A1, S2.3
  N10: Arduino_Nano_V3.A0, S1.3
  N11: Arduino_Nano_V3.D13/SCK, Part2.MISO
  VSS: U1.VSS, LCM1602_IIC2.VSS
  VDD: U1.VDD, LCM1602_IIC2.VDD
  N12: U1.VO, LCM1602_IIC2.V0
  N13: U1.RS, LCM1602_IIC2.RS
  N14: U1.R_W, LCM1602_IIC2.RW
  N15: U1.E, LCM1602_IIC2.E
  N16: U1.DB0, LCM1602_IIC2.D0
  N17: U1.DB1, LCM1602_IIC2.D1
  N18: U1.DB2, LCM1602_IIC2.D2
  N19: U1.DB3, LCM1602_IIC2.D3
  N20: U1.DB4, LCM1602_IIC2.D4
  N21: U1.DB5, LCM1602_IIC2.D5
  N22: U1.DB6, LCM1602_IIC2.D6
  N23: U1.DB7, LCM1602_IIC2.D7
  N24: U1.A, LCM1602_IIC2.A
  N25: U1.K, LCM1602_IIC2.K
  N26: 4N25.Pin_1, part.Pin_0

notes:
  3 - Motor
  1 - Ground
  2 - +5V
  4 - Read
  6 - Sense
  5 - Write
  Plus/4 provides +5V to board.
  WARNING: Do not connect the Arduino USB connector to power when connect to Plus/4!

custom parts:
  LCM1602 IIC: I2C-Module to use a 1602 or 2004 LCD on with the wire.h libory Serial LCD Modul
  4N25: Optocoupler
